# Fritzing sketch schematic (saved by Fritzing 0.9.10b)

parts:
  esp1 = ESP32 DevKitc V4
  Componente2 = HX711 Weighing Sensor Module
  Load_Cell1 = Load Cell - Red/white/black/green
  U1 = LCD-16X2 [package=lcd-16x2_noholes]
  LCM1602_IIC1 = LCM1602 IIC [part_number="LCM1602 IIC" chip_label="LCM1602 IIC" package="DIP (Dual Inline) [THT]"]
  S1 = Pushbutton [package="[THT]"]
  R1 = Resistor [tolerance=±5% power=0.25 resistance=220 package=THT]

nets:
  N1: esp1.IO18, Componente2.DO/RX
  N2: esp1.IO19, Componente2.CK/TX
  N3: esp1.IO21, LCM1602_IIC1.SDA
  N4: esp1.IO22, LCM1602_IIC1.SCL
  N5: esp1.IO27, S1.Pin_3, R1.Pin_1
  GND: esp1.GND, Componente2.GND, LCM1602_IIC1.GND, R1.Pin_0
  VCC: esp1.5V, Componente2.VCC, LCM1602_IIC1.VCC, S1.Pin_1
  N6: Componente2.E+, Load_Cell1.wire1
  N7: Componente2.E-, Load_Cell1.wire3
  N8: Componente2.A+, Load_Cell1.wire2
  N9: Componente2.A-, Load_Cell1.wire4
  VSS: U1.VSS, LCM1602_IIC1.VSS
  VDD: U1.VDD, LCM1602_IIC1.VDD
  N10: U1.VO, LCM1602_IIC1.V0
  N11: U1.RS, LCM1602_IIC1.RS
  N12: U1.R_W, LCM1602_IIC1.RW
  N13: U1.E, LCM1602_IIC1.E
  N14: U1.DB0, LCM1602_IIC1.D0
  N15: U1.DB1, LCM1602_IIC1.D1
  N16: U1.DB2, LCM1602_IIC1.D2
  N17: U1.DB3, LCM1602_IIC1.D3
  N18: U1.DB4, LCM1602_IIC1.D4
  N19: U1.DB5, LCM1602_IIC1.D5
  N20: U1.DB6, LCM1602_IIC1.D6
  N21: U1.DB7, LCM1602_IIC1.D7
  N22: U1.A, LCM1602_IIC1.A
  N23: U1.K, LCM1602_IIC1.K
  N24: LCM1602_IIC1.LED_A, LCM1602_IIC1.LED_B

custom parts:
  ESP32 DevKitc V4: ESP32-DevKitC board with ESP32-WROOM-32 module. ESP32-DevKitC V4 is a small-sized ESP32-based development board produced by Espressif. Most of the pins on the ESP module are broken out to the pin headers on the board. The pins D0, D1, D2, D3, CMD and CLK are used internally for communication between ESP32 and SPI flash memory. They are grouped on both sides near the USB connector. Avoid using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
  HX711 Weighing Sensor Module: HX711 is a precision 24-bit analog-to-digital converter (ADC) designed for weigh scales and industrial control applications to interface directly with a bridge sensor.
  Load Cell - Red/white/black/green: A rectangle load cell/weighting pressure Sensor with four wires - Red, white, black, green. Normally corresponding with E+, E-, A+, A- respectively.
  LCM1602 IIC: I2C-Module to use a 1602 or 2004 LCD on with the wire.h libory Serial LCD Modul
